# Fritzing sketch terminal_block (saved by Fritzing 0.9.3b)
circuit board: 1.4cm x 4.7cm
breadboards: 1

parts:
  5v_IN = Screw terminal - 2 pins [package=THT]
  J5 = Screw terminal - 2 pins [package=THT]
  J4 = Screw terminal - 2 pins [package=THT]
  J3 = Screw terminal - 2 pins [package=THT]
  J2 = Screw terminal - 2 pins [package=THT]

nets:
  N1: 5v_IN.pin1, J5.pin1, J4.pin1, J3.pin1, J2.pin1
  N2: 5v_IN.pin2, J5.pin2, J4.pin2, J3.pin2, J2.pin2

notes:
  1
  2
  3
  4
  5v IN
  Power Distribution
